// Digital circuit 1bit_add.dig as structural Verilog
module _1bit_add (
  input  I0,
  input  I1,
  input  CARRY_IN,
  output O,
  output CARRY_OUT
);

  wire and_1_out, and_2_out, xor_2_out;

  xor xor_1 (O, xor_2_out, CARRY_IN);
  xor xor_2 (xor_2_out, I1, I0);
  and and_1 (and_1_out, xor_2_out, CARRY_IN);
  and and_2 (and_2_out, I0, I1);
  or or_1 (CARRY_OUT, and_2_out, and_1_out);
endmodule
