// Digital circuit 8085.dig as structural Verilog
module _8085 (
  input  [2:0] in_1,
  input  INIT_CLK,
  input  INSTRUCT_CLK,
  input  CY_IN,
  input  FETCH_CLK,
  input  CLK,
  output [7:0] M_D,
  output [7:0] H_D,
  output [7:0] B_D,
  output [7:0] C_D,
  output [7:0] D_D,
  output [7:0] E_D,
  output [7:0] A_D,
  output CY,
  output OVF,
  output Z,
  output S,
  output [7:0] PC_plus_1,
  output [7:0] INSTRUCT
);

  wire and_1_out, and_2_out, and_3_out, and_4_out, and_5_out, delay_1_out, demultiplexer_1_out_0,
       demultiplexer_1_out_1, demultiplexer_1_out_2, demultiplexer_1_out_3, demultiplexer_1_out_4,
       demultiplexer_1_out_5, demultiplexer_1_out_6, demultiplexer_1_out_7,
       memory_initializer_1_mem_init_done, nand_1_out, not_1_out, not_2_out, not_3_out, not_4_out, not_5_out,
       or_2_out, or_3_out, undriven, undriven_2;
  wire [0:0] or_1_out;
  wire [2:0] DECODER_out;
  wire [3:0] byte_add_3_s;
  wire [7:0] BUF_o, byte_1_o, byte_2_o, byte_add_1_o, byte_add_2_o, byte_add_3_o, demultiplexer_2_out_0,
       demultiplexer_2_out_1, demultiplexer_2_out_2, demultiplexer_2_out_3, demultiplexer_2_out_4,
       demultiplexer_2_out_5, demultiplexer_2_out_6, demultiplexer_2_out_7, FLAGS_o, INSTRUCT_BUF_o,
       memory_initializer_1_o, multiplexer_1_out, multiplexer_2_out, multiplexer_3_out, multiplexer_4_out,
       multiplexer_5_out, multiplexer_6_out, multiplexer_7_out, multiplexer_8_out, PC_o, PC_plus_1_o;

  // counter counter_1: pin names not known; wires that end beside it: CLK, INSTRUCT_CLK, FETCH_CLK
  and and_1 (and_1_out, undriven_2, FLAGS_o[0]);
  or or_1 (or_1_out[0], FLAGS_o[0], memory_initializer_1_mem_init_done);
  LED MVI (.in(DECODER_out[2]));
  and and_2 (and_2_out, and_1_out, undriven);
  not not_1 (not_1_out, undriven);
  nand nand_1 (nand_1_out, and_1_out, undriven);
  and and_3 (and_3_out, and_1_out, not_1_out);
  \byte  INSTRUCTION (.SET(and_2_out), .I(INSTRUCT_BUF_o), .O(INSTRUCT));
  not not_2 (not_2_out, nand_1_out);
  byte_add byte_add_1 (.I0(PC_o), .I1(8'h1), .CARRY_IN(1'b0), .O(byte_add_1_o));  // open: CF, OF, Z, S
  \byte  byte_1 (.SET(not_2_out), .I(byte_add_1_o), .O(byte_1_o));
  Multiplexer #(.Bits(8)) multiplexer_1 (
    .sel(delay_1_out), .in_0({8{1'b0}}), .in_1({in_1, byte_add_3_s, or_1_out[0]}), .out(multiplexer_1_out));
  Delay #(.delayTime(2)) delay_1 (.in(1'b1), .out(delay_1_out));
  byte_add byte_add_2 (.I0(PC_o), .I1(8'h1), .CARRY_IN(1'b0), .O(byte_add_2_o));  // open: CF, OF, Z, S
  Multiplexer #(.Bits(8)) multiplexer_2 (
    .sel(demultiplexer_1_out_5), .in_0(byte_1_o), .in_1(demultiplexer_2_out_5), .out(multiplexer_2_out));
  \byte  u_PC_plus_1 (.SET(and_3_out), .I(byte_add_2_o), .O(PC_plus_1_o));
  \byte  FLAGS (.SET(1'b1), .I(multiplexer_1_out), .O({FLAGS_o[7:5], CY, OVF, Z, S, FLAGS_o[0]}));
  \byte  PC (.SET(nand_1_out), .I(multiplexer_2_out), .O(PC_o));
  Multiplexer #(.Bits(8)) multiplexer_3 (.sel(and_3_out), .in_0(PC_o), .in_1(PC_plus_1_o), .out(multiplexer_3_out));
  LookUpTable #(.Bits(3)) DECODER (.in0(INSTRUCT[6]), .in1(INSTRUCT[7]), .out(DECODER_out));
  Multiplexer #(.Bits(8)) multiplexer_4 (
    .sel(and_1_out), .in_0(H_D), .in_1(multiplexer_3_out), .out(multiplexer_4_out));
  \byte  CONSTANT (.SET(and_3_out), .I(INSTRUCT_BUF_o), .O(PC_plus_1));
  \byte  H (.SET(demultiplexer_1_out_6), .I(demultiplexer_2_out_6), .O(H_D));
  memory_initializer memory_initializer_1 (
    .DI(demultiplexer_2_out_7), .SET(demultiplexer_1_out_7), .ADDR(multiplexer_4_out),
    .MEM_INITD(FLAGS_o[0]), .INIT_CLK(INIT_CLK), .O(memory_initializer_1_o),
    .MEM_INIT_DONE(memory_initializer_1_mem_init_done));
  not not_3 (not_3_out, and_1_out);
  \byte  M_BUF (.SET(not_3_out), .I(memory_initializer_1_o), .O(M_D));
  \byte  INSTRUCT_BUF (.SET(and_1_out), .I(memory_initializer_1_o), .O(INSTRUCT_BUF_o));
  and and_4 (and_4_out, or_2_out, nand_1_out);
  or or_2 (or_2_out, DECODER_out[2], DECODER_out[0]);
  \byte  E (.SET(demultiplexer_1_out_4), .I(demultiplexer_2_out_4), .O(E_D));
  and and_5 (and_5_out, and_4_out, demultiplexer_1_out_0);
  \byte  D (.SET(demultiplexer_1_out_3), .I(demultiplexer_2_out_3), .O(D_D));
  or or_3 (or_3_out, DECODER_out[1], and_5_out);
  Multiplexer #(.Bits(8)) multiplexer_5 (
    .sel(or_3_out), .in_0({8{1'b0}}), .in_1(demultiplexer_2_out_0), .out(multiplexer_5_out));
  \byte  C (.SET(demultiplexer_1_out_2), .I(demultiplexer_2_out_2), .O(C_D));
  \byte  B (.SET(demultiplexer_1_out_1), .I(demultiplexer_2_out_1), .O(B_D));
  byte_add byte_add_3 (
    .I0(A_D), .I1(multiplexer_5_out), .CARRY_IN(CY_IN), .CF(byte_add_3_s[3]), .OF(byte_add_3_s[2]),
    .O(byte_add_3_o), .Z(byte_add_3_s[1]), .S(byte_add_3_s[0]));
  Multiplexer #(.Bits(8)) multiplexer_6 (
    .sel(and_5_out), .in_0(byte_add_3_o), .in_1(multiplexer_5_out), .out(multiplexer_6_out));
  \byte  byte_2 (.SET(nand_1_out), .I(multiplexer_6_out), .O(byte_2_o));
  not not_4 (not_4_out, nand_1_out);
  \byte  byte_3 (.SET(not_4_out), .I(byte_2_o), .O(A_D));
  Multiplexer #(.Selector_Bits(4), .Bits(8)) multiplexer_7 (
    .sel({1'b0, INSTRUCT[5:3]}), .in_0(A_D), .in_1(B_D), .in_2(C_D), .in_3(D_D), .in_4(E_D), .in_5(PC_o),
    .in_6(H_D), .in_7(M_D), .in_8(H_D), .in_9(INSTRUCT_BUF_o), .in_10({8{1'b0}}), .in_11({8{1'b0}}),
    .in_12({8{1'b0}}), .in_13({8{1'b0}}), .in_14({8{1'b0}}), .in_15({8{1'b0}}), .out(multiplexer_7_out));
  Demultiplexer #(.Selector_Bits(3)) demultiplexer_1 (
    .sel(INSTRUCT[2:0]), .in(and_4_out), .out_0(demultiplexer_1_out_0), .out_1(demultiplexer_1_out_1),
    .out_2(demultiplexer_1_out_2), .out_3(demultiplexer_1_out_3), .out_4(demultiplexer_1_out_4),
    .out_5(demultiplexer_1_out_5), .out_6(demultiplexer_1_out_6), .out_7(demultiplexer_1_out_7));
  not not_5 (not_5_out, and_4_out);
  Multiplexer #(.Bits(8)) multiplexer_8 (
    .sel(DECODER_out[2]), .in_0(multiplexer_7_out), .in_1({{5{1'b0}}, INSTRUCT[5:3]}), .out(multiplexer_8_out));
  \byte  BUF (.SET(not_5_out), .I(multiplexer_8_out), .O(BUF_o));
  Demultiplexer #(.Selector_Bits(3), .Bits(8)) demultiplexer_2 (
    .sel(INSTRUCT[2:0]), .in(BUF_o), .out_0(demultiplexer_2_out_0), .out_1(demultiplexer_2_out_1),
    .out_2(demultiplexer_2_out_2), .out_3(demultiplexer_2_out_3), .out_4(demultiplexer_2_out_4),
    .out_5(demultiplexer_2_out_5), .out_6(demultiplexer_2_out_6), .out_7(demultiplexer_2_out_7));

  // Notes on the sheet:
  //   INIT_CLK: Hz: 2147483647
  //   FETCH_CLK: Hz: 2
  //   CLK: Hz: 4
  //   contents of DECODER (hex, n*v repeats v):
  //   0,2,1,4
endmodule
