// Digital circuit acumulator.dig as structural Verilog
module acumulator (
  input  SET,
  input  [7:0] I,
  input  CLK,
  input  CY_IN,
  output [7:0] O,
  output CY,
  output OVF,
  output Z,
  output S
);

  wire not_1_out;
  wire [7:0] byte_1_o, byte_add_1_o, multiplexer_1_out;

  byte_add byte_add_1 (.I0(O), .I1(I), .CARRY_IN(CY_IN), .CF(CY), .OF(OVF), .O(byte_add_1_o), .Z(Z), .S(S));
  Multiplexer #(.Bits(8)) multiplexer_1 (.sel(SET), .in_0(byte_add_1_o), .in_1(I), .out(multiplexer_1_out));
  \byte  byte_1 (.SET(CLK), .I(multiplexer_1_out), .O(byte_1_o));
  not not_1 (not_1_out, CLK);
  \byte  byte_2 (.SET(not_1_out), .I(byte_1_o), .O(O));
endmodule
