// Digital circuit bit.dig as structural Verilog
module \bit  (
  input  IN,
  input  SET,
  output OUT,
  output nOUT
);

  wire nand_1_out, nand_2_out, not_1_out, reset_1_out;

  not not_1 (not_1_out, IN);
  nand nand_1 (nand_1_out, IN, SET);
  nand nand_2 (nand_2_out, SET, not_1_out);
  Reset reset_1 (.out(reset_1_out));
  nand nand_3 (OUT, nand_1_out, nOUT);
  nand nand_4 (nOUT, OUT, reset_1_out, nand_2_out);
endmodule
