// Digital circuit byte.dig as structural Verilog
module \byte  (
  input  SET,
  input  [7:0] I,
  output [7:0] O
);

  \bit  bit_1 (.IN(I[0]), .SET(SET), .OUT(O[0]));  // open: nOUT
  \bit  bit_2 (.IN(I[1]), .SET(SET), .OUT(O[1]));  // open: nOUT
  \bit  bit_3 (.IN(I[2]), .SET(SET), .OUT(O[2]));  // open: nOUT
  \bit  bit_4 (.IN(I[3]), .SET(SET), .OUT(O[3]));  // open: nOUT
  \bit  bit_5 (.IN(I[4]), .SET(SET), .OUT(O[4]));  // open: nOUT
  \bit  bit_6 (.IN(I[5]), .SET(SET), .OUT(O[5]));  // open: nOUT
  \bit  bit_7 (.IN(I[6]), .SET(SET), .OUT(O[6]));  // open: nOUT
  \bit  bit_8 (.IN(I[7]), .SET(SET), .OUT(O[7]));  // open: nOUT
endmodule
