// Digital circuit byte_add.dig as structural Verilog
module byte_add (
  input  [7:0] I0,
  input  [7:0] I1,
  input  CARRY_IN,
  output CF,
  output OF,
  output [7:0] O,
  output Z,
  output S
);

  wire _1bit_add_1_carry_out, _1bit_add_2_carry_out, _1bit_add_3_carry_out, _1bit_add_4_carry_out,
       _1bit_add_5_carry_out, _1bit_add_6_carry_out, _1bit_add_7_carry_out, or_1_out, or_2_out, or_3_out,
       or_4_out, or_5_out, or_6_out;

  _1bit_add _1bit_add_1 (.I0(I0[0]), .I1(I1[0]), .CARRY_IN(CARRY_IN), .O(O[0]), .CARRY_OUT(_1bit_add_1_carry_out));
  _1bit_add _1bit_add_2 (
    .I0(I0[1]), .I1(I1[1]), .CARRY_IN(_1bit_add_1_carry_out), .O(O[1]), .CARRY_OUT(_1bit_add_2_carry_out));
  or or_1 (or_1_out, O[1], O[0]);
  _1bit_add _1bit_add_3 (
    .I0(I0[2]), .I1(I1[2]), .CARRY_IN(_1bit_add_2_carry_out), .O(O[2]), .CARRY_OUT(_1bit_add_3_carry_out));
  or or_2 (or_2_out, or_3_out, or_1_out);
  _1bit_add _1bit_add_4 (
    .I0(I0[3]), .I1(I1[3]), .CARRY_IN(_1bit_add_3_carry_out), .O(O[3]), .CARRY_OUT(_1bit_add_4_carry_out));
  or or_3 (or_3_out, O[3], O[2]);
  _1bit_add _1bit_add_5 (
    .I0(I0[4]), .I1(I1[4]), .CARRY_IN(_1bit_add_4_carry_out), .O(O[4]), .CARRY_OUT(_1bit_add_5_carry_out));
  nor nor_1 (Z, or_5_out, or_2_out);
  _1bit_add _1bit_add_6 (
    .I0(I0[5]), .I1(I1[5]), .CARRY_IN(_1bit_add_5_carry_out), .O(O[5]), .CARRY_OUT(_1bit_add_6_carry_out));
  or or_4 (or_4_out, O[5], O[4]);
  _1bit_add _1bit_add_7 (
    .I0(I0[6]), .I1(I1[6]), .CARRY_IN(_1bit_add_6_carry_out), .O(O[6]), .CARRY_OUT(_1bit_add_7_carry_out));
  or or_5 (or_5_out, or_6_out, or_4_out);
  _1bit_add _1bit_add_8 (.I0(I0[7]), .I1(I1[7]), .CARRY_IN(_1bit_add_7_carry_out), .O(O[7]), .CARRY_OUT(CF));
  or or_6 (or_6_out, O[7], O[6]);
  xor xor_1 (OF, CF, _1bit_add_7_carry_out);

  assign S = O[7];
endmodule
