// Digital circuit counter.dig as structural Verilog
module counter (
  input  CLK,
  output CY,
  output [7:0] O
);

  wire not_1_out;
  wire [7:0] byte_1_o, byte_add_1_o;

  byte_add byte_add_1 (.I0(O), .I1(8'h1), .CARRY_IN(1'b0), .CF(CY), .O(byte_add_1_o));  // open: OF, Z, S
  \byte  byte_1 (.SET(CLK), .I(byte_add_1_o), .O(byte_1_o));
  not not_1 (not_1_out, CLK);
  \byte  byte_2 (.SET(not_1_out), .I(byte_1_o), .O(O));
endmodule
