// Digital circuit memory.dig as structural Verilog
module memory (
  input  [2:0] ADDR,
  input  SET,
  input  [7:0] I,
  output [7:0] O
);

  wire demultiplexer_2_out_0, demultiplexer_2_out_1, demultiplexer_2_out_2, demultiplexer_2_out_3,
       demultiplexer_2_out_4, demultiplexer_2_out_5, demultiplexer_2_out_6, demultiplexer_2_out_7;
  wire [7:0] byte_1_o, byte_2_o, byte_3_o, byte_4_o, byte_5_o, byte_6_o, byte_7_o, byte_8_o,
       demultiplexer_1_out_0, demultiplexer_1_out_1, demultiplexer_1_out_2, demultiplexer_1_out_3,
       demultiplexer_1_out_4, demultiplexer_1_out_5, demultiplexer_1_out_6, demultiplexer_1_out_7;

  Demultiplexer #(.Selector_Bits(3), .Bits(8)) demultiplexer_1 (
    .sel(ADDR), .in(I), .out_0(demultiplexer_1_out_0), .out_1(demultiplexer_1_out_1),
    .out_2(demultiplexer_1_out_2), .out_3(demultiplexer_1_out_3), .out_4(demultiplexer_1_out_4),
    .out_5(demultiplexer_1_out_5), .out_6(demultiplexer_1_out_6), .out_7(demultiplexer_1_out_7));
  Demultiplexer #(.Selector_Bits(3)) demultiplexer_2 (
    .sel(ADDR), .in(SET), .out_0(demultiplexer_2_out_0), .out_1(demultiplexer_2_out_1),
    .out_2(demultiplexer_2_out_2), .out_3(demultiplexer_2_out_3), .out_4(demultiplexer_2_out_4),
    .out_5(demultiplexer_2_out_5), .out_6(demultiplexer_2_out_6), .out_7(demultiplexer_2_out_7));
  \byte  byte_1 (.SET(demultiplexer_2_out_0), .I(demultiplexer_1_out_0), .O(byte_1_o));
  \byte  byte_2 (.SET(demultiplexer_2_out_1), .I(demultiplexer_1_out_1), .O(byte_2_o));
  \byte  byte_3 (.SET(demultiplexer_2_out_2), .I(demultiplexer_1_out_2), .O(byte_3_o));
  \byte  byte_4 (.SET(demultiplexer_2_out_3), .I(demultiplexer_1_out_3), .O(byte_4_o));
  \byte  byte_5 (.SET(demultiplexer_2_out_4), .I(demultiplexer_1_out_4), .O(byte_5_o));
  \byte  byte_6 (.SET(demultiplexer_2_out_5), .I(demultiplexer_1_out_5), .O(byte_6_o));
  \byte  byte_7 (.SET(demultiplexer_2_out_6), .I(demultiplexer_1_out_6), .O(byte_7_o));
  \byte  byte_8 (.SET(demultiplexer_2_out_7), .I(demultiplexer_1_out_7), .O(byte_8_o));
  Multiplexer #(.Selector_Bits(3), .Bits(8)) multiplexer_1 (
    .sel(ADDR), .in_0(byte_1_o), .in_1(byte_2_o), .in_2(byte_3_o), .in_3(byte_4_o), .in_4(byte_5_o),
    .in_5(byte_6_o), .in_6(byte_7_o), .in_7(byte_8_o), .out(O));
endmodule
