// Digital circuit memory_initializer.dig as structural Verilog
module memory_initializer (
  input  [7:0] DI,
  input  SET,
  input  [7:0] ADDR,
  input  MEM_INITD,
  input  INIT_CLK,
  output [7:0] O,
  output MEM_INIT_DONE
);

  wire and_1_out, not_1_out, or_1_out;
  wire [7:0] BOOTROM_d, counter_1_p2, multiplexer_1_out, multiplexer_2_out;

  ROM #(.AddrBits(8), .Bits(8)) BOOTROM (.A(multiplexer_2_out), .sel(1'b1), .D(BOOTROM_d));
  Multiplexer #(.Bits(8)) multiplexer_1 (.sel(MEM_INITD), .in_0(BOOTROM_d), .in_1(DI), .out(multiplexer_1_out));
  // counter counter_1: pin names not known; wires that end beside it: INIT_CLK, counter_1_p2, MEM_INIT_DONE
  not not_1 (not_1_out, MEM_INITD);
  and and_1 (and_1_out, not_1_out, INIT_CLK);
  or or_1 (or_1_out, and_1_out, SET);
  Multiplexer #(.Bits(8)) multiplexer_2 (.sel(MEM_INITD), .in_0(counter_1_p2), .in_1(ADDR), .out(multiplexer_2_out));
  RAMAsync #(.AddrBits(8), .Bits(8)) ramasync_1 (.A(multiplexer_2_out), .D(multiplexer_1_out), .we(or_1_out), .Q(O));

  // Notes on the sheet:
  //   INIT_CLK: Hz: 100
  //   contents of BOOTROM (hex, n*v repeats v):
  //   7,6,5,4,3,2,1
endmodule
