// Digital circuit select.dig as structural Verilog
module select (
  input  SELECT,
  input  IN0,
  input  IN1,
  output OUT
);

  wire and_1_out, and_2_out, not_1_out;

  and and_1 (and_1_out, IN0, not_1_out);
  not not_1 (not_1_out, SELECT);
  and and_2 (and_2_out, IN1, SELECT);
  or or_1 (OUT, and_1_out, and_2_out);
endmodule
